// Logisim project khalf adder.circ as structural Verilog: 1 circuit, main circuit main
module main (
  input  A,
  input  B,
  output S,
  output CARRY
);

  xor xor_1 (S, A, B);
  and and_1 (CARRY, A, B);
endmodule
